# Fritzing sketch Bluetooth Kontrollü Aracaın Fritzing Şeması (saved by Fritzing 0.9.3b)

parts:
  L298N1 = L298N DC motor driver
  Parça1 = Arduino Uno (Rev3) - ICSP
  U1 = BATTERY-2 [package=battery-aa]
  M2 = DC Motor
  VCC1 = Battery block 9V
  M4 = DC Motor
  M5 = DC Motor
  M6 = DC Motor
  U2 = BATTERY-2 [package=battery-aa]
  JACK1 = 2.1mm Barrel Jack with Terminal Block
  LED1 = LED - 3mm [color="Blue (430nm)" package="3 mm [THT]"]
  LED2 = LED - 3mm [color="Yellow (595nm)" package="3 mm [THT]"]
  LED3 = LED - 3mm [color="Red (633nm)" package="3 mm [THT]"]
  BT1 = Bluetooth HC-06u [package=THT]

nets:
  N1: L298N1.OUT1, M5.pin_2, M6.pin_2
  N2: L298N1.OUT2, M5.pin_1, M6.pin_1
  N3: L298N1.OUT3, M2.pin_2, M4.pin_2
  N4: L298N1.OUT4, M2.pin_1, M4.pin_1
  N5: L298N1.12V, U1.+1, U2.+1
  GND: L298N1.GND, Parça1.GND, U1.-1, U2.-1, LED3.cathode, BT1.GND
  N6: L298N1.5V#9, L298N1.ENA
  N7: L298N1.5V#10, L298N1.ENB
  N8: Parça1.D0/RX, BT1.TXD
  N9: Parça1.D1/TX, BT1.RXD
  N10: Parça1.D2, LED3.anode
  N11: Parça1.D3_PWM, LED2.anode
  N12: Parça1.D4, LED1.anode
  5V: Parça1.5V, BT1.VCC
  N13: VCC1.-, JACK1.NEG
  N14: VCC1.+, JACK1.POS

notes:
  Motor sürücü için güç kaynağı 2 x 12V pil
  Arduino için güç kaynağı 9V pil
  L298N motor sürücü kartı
  HC-06 Bluetooth modül

custom parts:
  L298N DC motor driver: 2x DC motor driver with 78M05 positive voltage regulator (7..35 V) L298N: max 46 V, 2 A Set 5 V Enable jumper to enable 5 V regultor (needed for the L298N) and +5 V output at screw terminal or supply external +5 V at screw terminal Set ENA and/or ENB to +5 V to enable motor permanently or supply ENA and/or ENB with PWM signal IN1 and IN2 set rotation directory for motor A (OUT1/OUT2) IN2 and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
  Bluetooth HC-06u: Bluetooth HC-06 - face up, pins down 16.5mm x 37.5mm PCB
